# Fritzing sketch Temperature (saved by Fritzing 0.8.7b)
breadboards: 1

parts:
  Part1 = Arduino Uno (Rev3) - ICSP
  R1 = Resistor [tolerance=±5% resistance=330 package=THT]
  LED1 = smd LED [color="Yellow (592nm)" package="1206 [SMD]"]
  R2 = Resistor [tolerance=±5% resistance=4.7k package=THT]
  U1 = mystery part, 3 pins [chip_label=?]
  R3 = Resistor [tolerance=±5% resistance=4.7k package=THT]
  U2 = mystery part, 3 pins [chip_label=?]

nets:
  N1: Part1.GND, R1.Pin_1, U1.pin1, U1.pin3, U2.pin1, U2.pin3
  N2: Part1.D5_PWM, R3.Pin_0, U2.pin2
  N3: Part1.D6_PWM, R2.Pin_0, U1.pin2
  N4: Part1.D7, LED1.cathode
  N5: Part1.5V, R2.Pin_1, R3.Pin_1
  N6: R1.Pin_0, LED1.anode
