# Fritzing sketch Temperature (saved by Fritzing 0.9.0b)
breadboards: 1

parts:
  Part1 = Arduino Uno (Rev3) - ICSP
  R1 = Resistor [tolerance=±5% resistance=330 package=THT]
  LED1 = smd LED [color="Yellow (592nm)" package="1206 [SMD]"]
  R2 = Resistor [tolerance=±5% resistance=4.7k package=THT]
  U1 = mystery part, 3 pins [chip_label=?]
  U2 = mystery part, 3 pins [chip_label=?]

nets:
  N1: Part1.5V, R2.Pin_1, U1.pin1, U2.pin1
  N2: Part1.D8, LED1.cathode
  N3: Part1.GND, R1.Pin_1, U1.pin3, U2.pin3
  N4: Part1.D7, R2.Pin_0, U1.pin2, U2.pin2
  N5: R1.Pin_0, LED1.anode
